# Fritzing sketch sensors (saved by Fritzing 0.9.3b)
breadboards: 1

parts:
  Part1 = Arduino Uno (Rev3) - ICSP
  R1 = Rotary Potentiometer (Large) [maximum_resistance=100kΩ package=THT]
  R2 = Resistor [tolerance=±5% resistance=10k package="0402 [SMD]"]
  R3 = PHOTOCELL [package=photocell-kit]

nets:
  N1: Part1.A0, R1.wiper
  N2: Part1.A1, R2.Pin_1, R3.P$1
  N3: Part1.5V, R1.leg1, R2.Pin_0
  N4: Part1.GND, R1.leg2, R3.P$2
