# Fritzing sketch motor_capacitive_sensor_and_pot (saved by Fritzing 0.9.3b)
breadboards: 1

parts:
  Part1 = Arduino Uno (Rev3) - ICSP
  R1 = Resistor [tolerance=±5% resistance=10M package="2010 [SMD]"]
  U1 = Voltage Regulator - 5V [package="DPak [SMD]"]
  M1 = DC Motor
  U2 = POT [package=pot_alpha_rv16af-20]  # not connected

nets:
  N1: Part1.D9_PWM, U1.input_voltage
  N2: Part1.D2, R1.Pin_1
  N3: Part1.D6_PWM, R1.Pin_0
  N4: Part1.5V, M1.pin_1
  N5: Part1.GND, U1.output_voltage
  N6: U1.GND, M1.pin_2
